# Fritzing sketch arduinoproject (saved by Fritzing 0.9.3b)
breadboards: 1

parts:
  부품1 = Arduino Uno (Rev3) - ICSP
  LED1 = smd LED [color="Red (633nm)" package="0805 [SMD]"]
  J1 = Piezo Speaker
  R1 = Resistor [tolerance=±5% resistance=220 package="1206 [SMD]"]
  R2 = Resistor [tolerance=±5% resistance=220 package="1206 [SMD]"]
  R3 = Temperature Sensor (Thermistor) [thermistor_type=NTC package=THT]
  R4 = Resistor [tolerance=±5% resistance=220 package="1206 [SMD]"]
  LED2 = smd LED [color="Red (633nm)" package="0805 [SMD]"]

nets:
  N1: 부품1.A0, R3.pin_1, R4.Pin_0
  N2: 부품1.D10_PWM/SS, R2.Pin_1
  N3: 부품1.D12/MISO, J1.pin2
  N4: 부품1.D13/SCK, R1.Pin_1
  N5: 부품1.5V, R3.pin_0
  N6: 부품1.GND, LED1.cathode, J1.pin1, R4.Pin_1, LED2.cathode
  N7: LED1.anode, R1.Pin_0
  N8: R2.Pin_0, LED2.anode
